// Logisim project ALU_project.circ as structural Verilog: 15 circuits, main circuit OneBitFullALU
module OneBitFullALU (
  input  S2,
  input  B,
  input  S0,
  input  S1,
  input  A,
  input  C_in,
  output G,
  output C_out
);

  wire arithmeticunit_1_sum, blogicunit_1_y_in, logicalunit_1_ou;

  Blogicunit blogicunit_1 (.B(B), .S0(S0), .S1(S1), .Y_in(blogicunit_1_y_in));
  ArithmeticUnit arithmeticunit_1 (
    .A(A), .Y_in(blogicunit_1_y_in), .C_in(C_in), .sum(arithmeticunit_1_sum), .C_out(C_out));
  LogicalUnit logicalunit_1 (.A(A), .B(B), .S1(S1), .S0(S0), .ou(logicalunit_1_ou));
  MUX mux_1 (.S2(S2), .ArUnit(arithmeticunit_1_sum), .LogUnit(logicalunit_1_ou), .G(G));

  // Notes on the sheet:
  //   1-bit ALU
  //   Y_in
endmodule

module HalfAdder (
  input  A,
  input  B,
  output sum,
  output carry
);

  xor xor_1 (sum, A, B);
  and and_1 (carry, A, B);

  // Notes on the sheet:
  //   XOR
  //   AND
endmodule

module FullAdder (
  input  A,
  input  B,
  input  C_in,
  output sum,
  output C_out
);

  wire and_1_out, and_2_out, xor_1_out;

  xor xor_1 (xor_1_out, A, B);
  and and_1 (and_1_out, A, B);
  xor xor_2 (sum, xor_1_out, C_in);
  and and_2 (and_2_out, xor_1_out, C_in);
  or or_1 (C_out, and_2_out, and_1_out);

  // Notes on the sheet:
  //   A
  //   B
  //   XOR
  //   AND
  //   AND
  //   OR
  //   C_out (S_1 and C_in) or C_1
endmodule

module CarryRipple (
  input  A_0,
  input  B_0,
  input  C_0___0,
  input  A_1,
  input  B_1,
  input  A_2,
  input  B_2,
  input  A_3,
  input  B_3,
  output sum,
  output out_11,
  output sum_2,
  output out_13,
  output sum_3,
  output out_15,
  output sum_4,
  output out_17
);

  wire and_1_out, and_2_out, and_3_out, and_4_out, and_5_out, and_6_out, and_7_out, and_8_out, xor_1_out,
       xor_2_out, xor_3_out, xor_4_out;

  xor xor_1 (xor_1_out, A_0, B_0);
  and and_1 (and_1_out, A_0, B_0);
  xor xor_2 (xor_2_out, A_1, B_1);
  and and_2 (and_2_out, A_1, B_1);
  xor xor_3 (xor_3_out, A_2, B_2);
  and and_3 (and_3_out, A_2, B_2);
  xor xor_4 (xor_4_out, A_3, B_3);
  and and_4 (and_4_out, A_3, B_3);
  xor xor_5 (sum, xor_1_out, C_0___0);
  and and_5 (and_5_out, xor_1_out, C_0___0);
  xor xor_6 (sum_2, xor_2_out, out_11);
  xor xor_7 (sum_3, xor_3_out, out_13);
  xor xor_8 (sum_4, xor_4_out, out_15);
  and and_6 (and_6_out, xor_2_out, out_11);
  and and_7 (and_7_out, xor_3_out, out_13);
  and and_8 (and_8_out, xor_4_out, out_15);
  or or_1 (out_13, and_6_out, and_2_out);
  or or_2 (out_15, and_7_out, and_3_out);
  or or_3 (out_17, and_8_out, and_4_out);
  or or_4 (out_11, and_5_out, and_1_out);

  // Notes on the sheet:
  //   C_1
  //   C_2
  //   C_3
  //   XOR
  //   sum of A, B
  //   AND
  //   AND
  //   AND
  //   AND
  //   AND
  //   cary of A+B
  //   XOR
  //   AND
  //   AND
  //   AND
  //   carry_temp=sum and carry0
  //   OR
  //   OR
  //   OR
  //   OR
  //   final carry = C_2
  //   final carry = C_3
  //   final carry = C_4
  //   final carry = C_1
endmodule

module Blogicunit (
  input  B,
  input  S0,
  input  S1,
  output Y_in
);

  wire and_1_out, and_2_out, not_1_out;

  not not_1 (not_1_out, B);
  and and_1 (and_1_out, B, S0);
  and and_2 (and_2_out, not_1_out, S1);
  or or_1 (Y_in, and_1_out, and_2_out);
endmodule

module ArithmeticUnit (
  input  A,
  input  Y_in,
  input  C_in,
  output sum,
  output C_out
);

  wire and_1_out, and_2_out, xor_1_out;

  xor xor_1 (xor_1_out, A, Y_in);
  and and_1 (and_1_out, A, Y_in);
  xor xor_2 (sum, xor_1_out, C_in);
  and and_2 (and_2_out, xor_1_out, C_in);
  or or_1 (C_out, and_2_out, and_1_out);

  // Notes on the sheet:
  //   XOR
  //   AND
  //   AND
  //   OR
  //   C_out (S_1 and C_in) or C_1
endmodule

module BLogicAndArithmeticUnits (
  input  B,
  input  S0,
  input  S1,
  input  A,
  input  C_in,
  output out_6,
  output sum,
  output out_8
);

  wire and_1_out, and_2_out, and_3_out, and_4_out, not_1_out, xor_1_out;

  not not_1 (not_1_out, B);
  and and_1 (and_1_out, B, S0);
  xor xor_1 (xor_1_out, A, out_6);
  and and_2 (and_2_out, A, out_6);
  and and_3 (and_3_out, not_1_out, S1);
  or or_1 (out_6, and_1_out, and_3_out);
  xor xor_2 (sum, xor_1_out, C_in);
  and and_4 (and_4_out, xor_1_out, C_in);
  or or_2 (out_8, and_4_out, and_2_out);

  // Notes on the sheet:
  //   Y_in
  //   B-input logic (1 bit)
  //   Arithmetic Unit
  //   XOR
  //   AND
  //   Y_in
  //   AND
  //   OR
  //   C_out (S_1 and C_in) or C_1
endmodule

module BLogicUnitNBITS (
  input  [3:0] B,
  input  S0,
  input  S1,
  output [3:0] Y_in
);

  wire [3:0] and_1_out, and_2_out, bit_extender_1_out, bit_extender_2_out, not_1_out;

  assign not_1_out = ~B;  // NOT_Gate not_1, 4 bits wide
  assign bit_extender_1_out = {{3{S0}}, S0};  // Bit_Extender bit_extender_1
  assign bit_extender_2_out = {{3{S1}}, S1};  // Bit_Extender bit_extender_2
  assign and_1_out = B & bit_extender_1_out;  // AND_Gate and_1, 4 bits wide
  assign and_2_out = not_1_out & bit_extender_2_out;  // AND_Gate and_2, 4 bits wide
  assign Y_in = and_1_out | and_2_out;  // OR_Gate or_1, 4 bits wide

  // Notes on the sheet:
  //   B-logic_n-bits
endmodule

module ArithmeticUnitNBITS (
  input  A0,
  input  B0,
  input  Cin,
  input  A1,
  input  B1,
  input  A2,
  input  B2,
  input  A3,
  input  B3,
  output sum0,
  output sum1,
  output sum2,
  output sum3,
  output C_out
);

  wire and_1_out, and_2_out, and_3_out, and_4_out, and_5_out, and_6_out, and_7_out, and_8_out, or_2_out,
       or_3_out, or_4_out, xor_1_out, xor_2_out, xor_3_out, xor_4_out;

  xor xor_1 (xor_1_out, A0, B0);
  xor xor_2 (xor_2_out, A1, B1);
  xor xor_3 (xor_3_out, A2, B2);
  xor xor_4 (xor_4_out, A3, B3);
  and and_1 (and_1_out, A3, B3);
  and and_2 (and_2_out, A0, B0);
  and and_3 (and_3_out, A1, B1);
  and and_4 (and_4_out, A2, B2);
  and and_5 (and_5_out, xor_1_out, Cin);
  xor xor_5 (sum0, xor_1_out, Cin);
  xor xor_6 (sum1, xor_2_out, or_4_out);
  xor xor_7 (sum2, xor_3_out, or_2_out);
  xor xor_8 (sum3, xor_4_out, or_3_out);
  and and_6 (and_6_out, xor_2_out, or_4_out);
  and and_7 (and_7_out, xor_3_out, or_2_out);
  and and_8 (and_8_out, xor_4_out, or_3_out);
  or or_1 (C_out, and_8_out, and_1_out);
  or or_2 (or_2_out, and_6_out, and_3_out);
  or or_3 (or_3_out, and_7_out, and_4_out);
  or or_4 (or_4_out, and_5_out, and_2_out);

  // Notes on the sheet:
  //   C_3
  //   XOR
  //   AND
  //   AND
  //   AND
  //   AND
  //   sum of A, B
  //   cary of A+B
  //   XOR
  //   AND
  //   carry_temp=sum and carry0
  //   AND
  //   AND
  //   AND
  //   OR
  //   OR
  //   OR
  //   OR
  //   final carry = C_3
  //   final carry = C_4
  //   final carry = C_1
  //   final carry = C_2
endmodule

module LogicalUnit (
  input  A,
  input  B,
  input  S1,
  input  S0,
  output ou
);

  wire and_1_out, and_2_out, and_3_out, and_4_out, and_5_out, not_1_out, not_2_out, not_3_out, or_1_out,
       xor_1_out;

  not not_1 (not_1_out, S1);
  not not_2 (not_2_out, S0);
  and and_1 (and_1_out, A, B);
  or or_1 (or_1_out, A, B);
  xor xor_1 (xor_1_out, A, B);
  not not_3 (not_3_out, A);
  and and_2 (and_2_out, and_1_out, not_1_out, not_2_out);
  and and_3 (and_3_out, or_1_out, not_1_out, S0);
  and and_4 (and_4_out, xor_1_out, S1, not_2_out);
  and and_5 (and_5_out, not_3_out, S1, S0);
  or or_2 (ou, and_2_out, and_3_out, and_4_out, and_5_out);

  // Notes on the sheet:
  //   B
  //   Logical Unit (1-bit)
  //   Output=negS1​negS0​(A∧B)∨negS1​S0​(A∨B)∨S1​negS0​(A⊕B)∨S1​S0​(negA)
endmodule

module LogicUnitNBITS (
  input  [3:0] A,
  input  [3:0] B,
  input  S1,
  input  S0,
  output [3:0] ou
);

  wire [3:0] and_1_out, and_2_out, and_3_out, and_4_out, and_5_out, bit_extender_1_out, bit_extender_2_out,
       not_1_out, not_2_out, not_3_out, or_1_out, xor_1_out;

  assign bit_extender_1_out = {{3{S1}}, S1};  // Bit_Extender bit_extender_1
  assign bit_extender_2_out = {{3{S0}}, S0};  // Bit_Extender bit_extender_2
  assign not_1_out = ~bit_extender_1_out;  // NOT_Gate not_1, 4 bits wide
  assign not_2_out = ~bit_extender_2_out;  // NOT_Gate not_2, 4 bits wide
  assign and_1_out = A & B;  // AND_Gate and_1, 4 bits wide
  assign or_1_out = A | B;  // OR_Gate or_1, 4 bits wide
  assign xor_1_out = A ^ B;  // XOR_Gate xor_1, 4 bits wide
  assign not_3_out = ~A;  // NOT_Gate not_3, 4 bits wide
  assign and_2_out = and_1_out & not_1_out & not_2_out;  // AND_Gate and_2, 4 bits wide
  assign and_3_out = or_1_out & not_1_out & bit_extender_2_out;  // AND_Gate and_3, 4 bits wide
  assign and_4_out = xor_1_out & bit_extender_1_out & not_2_out;  // AND_Gate and_4, 4 bits wide
  assign and_5_out = not_3_out & bit_extender_1_out & bit_extender_2_out;  // AND_Gate and_5, 4 bits wide
  assign ou = and_2_out | and_3_out | and_4_out | and_5_out;  // OR_Gate or_2, 4 bits wide

  // Notes on the sheet:
  //   Logical Unit (n-bit)
  //   Output=negS1​negS0​(A∧B)∨negS1​S0​(A∨B)∨S1​negS0​(A⊕B)∨S1​S0​(negA)
endmodule

module MUX (
  input  S2,
  input  ArUnit,
  input  LogUnit,
  output G
);

  wire and_1_out, and_2_out, not_1_out;

  not not_1 (not_1_out, S2);
  and and_1 (and_1_out, S2, LogUnit);
  and and_2 (and_2_out, ArUnit, not_1_out);
  or or_1 (G, and_1_out, and_2_out);

  // Notes on the sheet:
  //   Output = LogUnit * S2 + ArUnit * negS2
endmodule

module NBITsFullALU (
  input  [3:0] B,
  input  S1,
  input  S0,
  input  A0,
  input  S2,
  input  Cin,
  input  A1,
  input  A2,
  input  A3,
  output [3:0] out_10,
  output C_out
);

  wire [3:0] Arithmetic_Unit_sum0, B_Logic_Unit_y_in, Logic_Unit_ou;

  BLogicUnitNBITS B_Logic_Unit (.B(B), .S0(S0), .S1(S1), .Y_in(B_Logic_Unit_y_in));
  ArithmeticUnitNBITS Arithmetic_Unit (
    .A0(A0), .B0(B_Logic_Unit_y_in[0]), .Cin(Cin), .A1(A1), .B1(B_Logic_Unit_y_in[1]), .A2(A2),
    .B2(B_Logic_Unit_y_in[2]), .A3(A3), .B3(B_Logic_Unit_y_in[3]), .sum0(Arithmetic_Unit_sum0[0]),
    .sum1(Arithmetic_Unit_sum0[1]), .sum2(Arithmetic_Unit_sum0[2]), .sum3(Arithmetic_Unit_sum0[3]),
    .C_out(C_out));
  LogicUnitNBITS Logic_Unit (.A({A0, A1, A2, A3}), .B(B), .S1(S1), .S0(S0), .ou(Logic_Unit_ou));
  MUXNBITS MUX (.S2(S2), .ArUnit(Arithmetic_Unit_sum0), .LogicUnit(Logic_Unit_ou), .G(out_10));
endmodule

module MUXNBITS (
  input  S2,
  input  [3:0] ArUnit,
  input  [3:0] LogicUnit,
  output [3:0] G
);

  wire [3:0] and_1_out, and_2_out, bit_extender_1_out, not_1_out;

  assign not_1_out = ~bit_extender_1_out;  // NOT_Gate not_1, 4 bits wide
  assign bit_extender_1_out = {{3{S2}}, S2};  // Bit_Extender bit_extender_1
  assign and_1_out = bit_extender_1_out & LogicUnit;  // AND_Gate and_1, 4 bits wide
  assign and_2_out = ArUnit & not_1_out;  // AND_Gate and_2, 4 bits wide
  assign G = and_1_out | and_2_out;  // OR_Gate or_1, 4 bits wide

  // Notes on the sheet:
  //   Output = LogUnit * S2 + ArUnit * negS2
endmodule

module CarryRipple_block_diagram (
  input  A0,
  input  B0,
  input  C0,
  input  A1,
  input  B1,
  input  A2,
  input  B2,
  input  A3,
  input  A4,
  output sum0,
  output sum1,
  output sum2,
  output sum3,
  output C_out
);

  wire fulladder_1_c_out, fulladder_2_c_out, fulladder_3_c_out;

  FullAdder fulladder_1 (.A(A0), .B(B0), .C_in(C0), .sum(sum0), .C_out(fulladder_1_c_out));
  FullAdder fulladder_2 (.A(A1), .B(B1), .C_in(fulladder_1_c_out), .sum(sum1), .C_out(fulladder_2_c_out));
  FullAdder fulladder_3 (.A(A2), .B(B2), .C_in(fulladder_2_c_out), .sum(sum2), .C_out(fulladder_3_c_out));
  FullAdder fulladder_4 (.A(A3), .B(A4), .C_in(fulladder_3_c_out), .sum(sum3), .C_out(C_out));
endmodule
